# Fritzing sketch EUI_board (saved by Fritzing 0.9.2b)
circuit board: 14.4524cm x 6.94637cm
breadboards: 1

parts:
  Teensy1 = Teensy 3.0
  R1 = Resistor [tolerance=±5% resistance=1k package=THT]
  R2 = Resistor [tolerance=±5% resistance=1k package=THT]
  R3 = Resistor [tolerance=±5% resistance=1k package=THT]
  R4 = Resistor [tolerance=±5% resistance=1k package=THT]
  R5 = Resistor [tolerance=±5% resistance=1k package=THT]
  R6 = Resistor [tolerance=±5% resistance=1k package=THT]
  R7 = Resistor [tolerance=±5% resistance=1k package=THT]
  R8 = Resistor [tolerance=±5% resistance=1k package=THT]
  LED_Connector_1 = double row female pin header, 10 pins [form="♀ (female)"]
  LED_Connector_2 = double row female pin header, 10 pins [form="♀ (female)"]
  R9 = Resistor [tolerance=±5% resistance=1k package=THT]
  R10 = Resistor [tolerance=±5% resistance=1k package=THT]
  R11 = Resistor [tolerance=±5% resistance=1k package=THT]
  R12 = Resistor [tolerance=±5% resistance=1k package=THT]
  R13 = Resistor [tolerance=±5% resistance=1k package=THT]
  R14 = Resistor [tolerance=±5% resistance=1k package=THT]
  R15 = Resistor [tolerance=±5% resistance=1k package=THT]
  R16 = Resistor [tolerance=±5% resistance=1k package=THT]
  J3 = female pin header, 8 pins [form="♀ (female)"]
  R17 = Resistor [tolerance=±5% resistance=220 package=THT]
  R18 = Resistor [tolerance=±5% resistance=220 package=THT]
  R19 = Resistor [tolerance=±5% resistance=220 package=THT]
  R20 = Resistor [tolerance=±5% resistance=220 package=THT]
  R21 = Resistor [tolerance=±5% resistance=220 package=THT]
  R23 = Resistor [tolerance=±5% resistance=220 package=THT]
  R22 = Resistor [tolerance=±5% resistance=220 package=THT]
  Sensor_Connector_1 = double row female pin header, 12 pins [form="♀ (female)"]
  +3_3V = female pin header, 1 pin [form="♀ (female)"]
  Sensor_Connector_2 = double row female pin header, 12 pins [form="♀ (female)"]
  +3_3V1 = female pin header, 1 pin [form="♀ (female)"]
  C2 = Tantalum Capacitor [capacitance=1μF package="200 mil [THT, tantalum]"]
  C3 = Tantalum Capacitor [capacitance=1μF package="200 mil [THT, tantalum]"]
  AREF = female pin header, 1 pin [form="♀ (female)"]
  J6 = female pin header, 1 pin [form="♀ (female)"]
  J7 = female pin header, 1 pin [form="♀ (female)"]
  J9 = female pin header, 1 pin [form="♀ (female)"]
  J10 = female pin header, 1 pin [form="♀ (female)"]
  J11 = female pin header, 1 pin [form="♀ (female)"]
  part = female pin header, 1 pin [form="♀ (female)"]
  A10_&_A11 = female pin header, 2 pins [form="♀ (female)"]
  R24 = Resistor [tolerance=±5% resistance=220 package=THT]
  R25 = Resistor [tolerance=±5% resistance=220 package=THT]

nets:
  N1: Teensy1.GND, LED_Connector_1.pin8, LED_Connector_1.pin9, LED_Connector_2.pin2, LED_Connector_2.pin3, R17.Pin_1, R18.Pin_1, R19.Pin_1, R20.Pin_1, R21.Pin_1, R23.Pin_1, R22.Pin_1, C2.+, C3.+, J6.pin1, J7.pin1, part.pin1, R24.Pin_0, R25.Pin_0
  N2: Teensy1.D0, R1.Pin_0
  N3: Teensy1.D1, R2.Pin_0
  N4: Teensy1.D2, R3.Pin_0
  N5: Teensy1.D3, R4.Pin_0
  N6: Teensy1.D4, R5.Pin_0
  N7: Teensy1.D5, R6.Pin_0
  N8: Teensy1.D6, R7.Pin_0
  N9: Teensy1.D7, R8.Pin_0
  N10: Teensy1.3V3#15, Sensor_Connector_2.pin7, Sensor_Connector_2.pin8, Sensor_Connector_2.pin9, Sensor_Connector_2.pin10, Sensor_Connector_2.pin11, Sensor_Connector_2.pin12
  N11: Teensy1.A0/D14, Sensor_Connector_2.pin4, J9.pin1
  N12: Teensy1.A1/D15, Sensor_Connector_2.pin3, J10.pin1
  N13: Teensy1.A2/D16, Sensor_Connector_2.pin2, J11.pin1
  N14: Teensy1.A3/D17, R23.Pin_0, Sensor_Connector_2.pin1
  N15: Teensy1.A4/D18, R22.Pin_0, Sensor_Connector_1.pin12
  N16: Teensy1.A5/D19, R21.Pin_0, Sensor_Connector_1.pin11
  N17: Teensy1.A6/D20, R20.Pin_0, Sensor_Connector_1.pin10
  N18: Teensy1.A7/D21, R19.Pin_0, Sensor_Connector_1.pin9
  N19: Teensy1.A8/D22, R18.Pin_0, Sensor_Connector_1.pin8
  N20: Teensy1.A9/D23, R17.Pin_0, Sensor_Connector_1.pin7
  N21: Teensy1.3V3#30, +3_3V1.pin1
  N22: R1.Pin_1, LED_Connector_1.pin7
  N23: R2.Pin_1, LED_Connector_1.pin6
  N24: R3.Pin_1, LED_Connector_1.pin5
  N25: R4.Pin_1, LED_Connector_1.pin4
  N26: R5.Pin_1, LED_Connector_1.pin3
  N27: R6.Pin_1, LED_Connector_1.pin2
  N28: R7.Pin_1, LED_Connector_1.pin1
  N29: R8.Pin_1, LED_Connector_1.pin10
  N30: LED_Connector_2.pin1, R9.Pin_0
  N31: LED_Connector_2.pin4, R16.Pin_0
  N32: LED_Connector_2.pin5, R15.Pin_0
  N33: LED_Connector_2.pin6, R14.Pin_0
  N34: LED_Connector_2.pin7, R13.Pin_0
  N35: LED_Connector_2.pin8, R12.Pin_0
  N36: LED_Connector_2.pin9, R11.Pin_0
  N37: LED_Connector_2.pin10, R10.Pin_0
  N38: R9.Pin_1, J3.pin1
  N39: R10.Pin_1, J3.pin2
  N40: R11.Pin_1, J3.pin3
  N41: R12.Pin_1, J3.pin4
  N42: R13.Pin_1, J3.pin5
  N43: R14.Pin_1, J3.pin6
  N44: R15.Pin_1, J3.pin7
  N45: R16.Pin_1, J3.pin8
  N46: Sensor_Connector_1.pin1, Sensor_Connector_1.pin2, Sensor_Connector_1.pin3, Sensor_Connector_1.pin4, Sensor_Connector_1.pin5, Sensor_Connector_1.pin6, +3_3V.pin1
  N47: Sensor_Connector_2.pin5, A10_&_A11.pin1, R25.Pin_1
  N48: Sensor_Connector_2.pin6, A10_&_A11.pin2, R24.Pin_1
  N49: C2.-, C3.-, AREF.pin1

notes:
  GND
