# Fritzing sketch EUI_board_recover (saved by Fritzing 0.9.0b)
circuit board: 14.4524cm x 6.94637cm
breadboards: 1

parts:
  R1 = Resistor [tolerance=±5% resistance=100 package=THT]
  R2 = Resistor [tolerance=±5% resistance=100 package=THT]
  R3 = Resistor [tolerance=±5% resistance=100 package=THT]
  R4 = Resistor [tolerance=±5% resistance=100 package=THT]
  R5 = Resistor [tolerance=±5% resistance=100 package=THT]
  R6 = Resistor [tolerance=±5% resistance=100 package=THT]
  R7 = Resistor [tolerance=±5% resistance=100 package=THT]
  R8 = Resistor [tolerance=±5% resistance=100 package=THT]
  LED_Connector_1 = double row female pin header, 10 pins [form="♀ (female)"]
  LED_Connector_2 = double row female pin header, 10 pins [form="♀ (female)"]
  R9 = Resistor [tolerance=±5% resistance=100 package=THT]
  R10 = Resistor [tolerance=±5% resistance=100 package=THT]
  R11 = Resistor [tolerance=±5% resistance=100 package=THT]
  R12 = Resistor [tolerance=±5% resistance=100 package=THT]
  R13 = Resistor [tolerance=±5% resistance=100 package=THT]
  R14 = Resistor [tolerance=±5% resistance=100 package=THT]
  R15 = Resistor [tolerance=±5% resistance=100 package=THT]
  R16 = Resistor [tolerance=±5% resistance=100 package=THT]
  J3 = female pin header, 8 pins [form="♀ (female)"]
  R17 = Resistor [tolerance=±5% resistance=220 package=THT]
  R18 = Resistor [tolerance=±5% resistance=220 package=THT]
  R19 = Resistor [tolerance=±5% resistance=220 package=THT]
  R20 = Resistor [tolerance=±5% resistance=220 package=THT]
  R23 = Resistor [tolerance=±5% resistance=100 package=THT]
  Sensor_Connector_1 = double row female pin header, 12 pins [form="♀ (female)"]
  Sensor_Connector_2 = double row female pin header, 12 pins [form="♀ (female)"]
  C2 = Tantalum Capacitor [capacitance=1μF package="200 mil [THT, tantalum]"]
  C3 = Tantalum Capacitor [capacitance=1μF package="200 mil [THT, tantalum]"]
  AREF = female pin header, 1 pin [form="♀ (female)"]
  J10 = female pin header, 1 pin [form="♀ (female)"]
  A10_&_A11 = female pin header, 2 pins [form="♀ (female)"]
  R24 = Resistor [tolerance=±5% resistance=100 package=THT]
  R25 = Resistor [tolerance=±5% resistance=100 package=THT]
  R21 = Resistor [tolerance=±5% resistance=220 package=THT]
  R22 = Resistor [tolerance=±5% resistance=100 package=THT]
  J11 = female pin header, 1 pin [form="♀ (female)"]
  J7 = female pin header, 1 pin [form="♀ (female)"]
  J6 = female pin header, 1 pin [form="♀ (female)"]
  J12 = female pin header, 1 pin [form="♀ (female)"]
  J12_2 = female pin header, 1 pin [form="♀ (female)"]
  J9 = female pin header, 1 pin [form="♀ (female)"]
  R26 = Resistor [tolerance=±5% resistance=100 package=THT]  # not connected
  R27 = Resistor [tolerance=±5% resistance=100 package=THT]  # not connected
  R28 = Resistor [tolerance=±5% resistance=100 package=THT]  # not connected
  Teensy1 = Teensy 3.0

nets:
  N1: R1.Pin_0, Teensy1.D0
  N2: R1.Pin_1, LED_Connector_1.pin7
  N3: R2.Pin_0, Teensy1.D1
  N4: R2.Pin_1, LED_Connector_1.pin6
  N5: R3.Pin_0, Teensy1.D2
  N6: R3.Pin_1, LED_Connector_1.pin5
  N7: R4.Pin_0, Teensy1.D3
  N8: R4.Pin_1, LED_Connector_1.pin4
  N9: R5.Pin_0, Teensy1.D4
  N10: R5.Pin_1, LED_Connector_1.pin3
  N11: R6.Pin_0, Teensy1.D5
  N12: R6.Pin_1, LED_Connector_1.pin2
  N13: R7.Pin_0, Teensy1.D6
  N14: R7.Pin_1, LED_Connector_1.pin1
  N15: R8.Pin_0, Teensy1.D7
  N16: R8.Pin_1, LED_Connector_1.pin10
  N17: LED_Connector_1.pin8, LED_Connector_1.pin9, LED_Connector_2.pin2, LED_Connector_2.pin3, R17.Pin_1, R18.Pin_1, R19.Pin_1, R20.Pin_1, R23.Pin_1, C2.+, C3.+, R24.Pin_0, R25.Pin_0, R21.Pin_1, R22.Pin_1, J7.pin1, J6.pin1, J12.pin1, J12_2.pin1, Teensy1.GND
  N18: LED_Connector_2.pin1, R9.Pin_0
  N19: LED_Connector_2.pin4, R16.Pin_0
  N20: LED_Connector_2.pin5, R15.Pin_0
  N21: LED_Connector_2.pin6, R14.Pin_0
  N22: LED_Connector_2.pin7, R13.Pin_0
  N23: LED_Connector_2.pin8, R12.Pin_0
  N24: LED_Connector_2.pin9, R11.Pin_0
  N25: LED_Connector_2.pin10, R10.Pin_0
  N26: R9.Pin_1, J3.pin1
  N27: R10.Pin_1, J3.pin2
  N28: R11.Pin_1, J3.pin3
  N29: R12.Pin_1, J3.pin4
  N30: R13.Pin_1, J3.pin5
  N31: R14.Pin_1, J3.pin6
  N32: R15.Pin_1, J3.pin7
  N33: R16.Pin_1, J3.pin8
  N34: R17.Pin_0, Sensor_Connector_1.pin7, Teensy1.A9/D23
  N35: R18.Pin_0, Sensor_Connector_1.pin8, Teensy1.A8/D22
  N36: R19.Pin_0, Sensor_Connector_1.pin9, Teensy1.A7/D21
  N37: R20.Pin_0, Sensor_Connector_1.pin10, Teensy1.A6/D20
  N38: R23.Pin_0, Sensor_Connector_2.pin1, Teensy1.A3/D17
  N39: Sensor_Connector_1.pin1, Sensor_Connector_1.pin2, Sensor_Connector_1.pin3, Sensor_Connector_1.pin4, Sensor_Connector_1.pin5, Sensor_Connector_1.pin6, Teensy1.3V3#30
  N40: Sensor_Connector_1.pin11, R21.Pin_0, Teensy1.A5/D19
  N41: Sensor_Connector_1.pin12, R22.Pin_0, Teensy1.A4/D18
  N42: Sensor_Connector_2.pin2, J11.pin1, Teensy1.A2/D16
  N43: Sensor_Connector_2.pin3, J10.pin1, Teensy1.A1/D15
  N44: Sensor_Connector_2.pin4, J9.pin1, Teensy1.A0/D14
  N45: Sensor_Connector_2.pin5, A10_&_A11.pin1, R25.Pin_1
  N46: Sensor_Connector_2.pin6, A10_&_A11.pin2, R24.Pin_1
  N47: Sensor_Connector_2.pin7, Sensor_Connector_2.pin8, Sensor_Connector_2.pin9, Sensor_Connector_2.pin10, Sensor_Connector_2.pin11, Sensor_Connector_2.pin12, Teensy1.3V3#15
  N48: C2.-, C3.-, AREF.pin1

notes:
  GND
